# Fritzing sketch Wiring (saved by Fritzing 0.9.5d)

parts:
  part = Raspberry Pi 3 [part_number="ReRAM RPi"]
  part_2 = Raspberry Pi 3 [part_number="Collector RPi"]
  J3 = double row male pin header, 32 pins [form="♂ (male)"]  # not connected
  ReRAM_PCB = double row male pin header, 32 pins [form="♂ (male)"]  # not connected
  J2 = double row male pin header, 32 pins [form="♂ (male)"]
  J1 = double row male pin header, 32 pins [form="♂ (male)"]
  J5 = female pin header, 2 pins [form="♀ (female)"]  # not connected
  J6 = female pin header, 2 pins [form="♀ (female)"]  # not connected
  J7 = female pin header, 2 pins [form="♀ (female)"]  # not connected
  J8 = female pin header, 2 pins [form="♀ (female)"]  # not connected

nets:
  3V3: part.3v3, part.3V3, J2.pin4, J1.pin1
  GND: part.GND, part_2.GND, J2.pin6
  N1: part.GPIO10, J1.pin4
  N2: part.GPIO9, J2.pin3
  N3: part.GPIO11, J1.pin3
  N4: part.GPIO8, J2.pin2
  N5: part.GPIO25, J2.pin5
  N6: part.GPIO15, part_2.GPIO14
  N7: part.GPIO14, part_2.GPIO15

notes:
  3V
  GND
  PF6/CS!
